# Fritzing sketch wiring (saved by Fritzing 1.0.7)
perfboards: 1

parts:
  Part1 = InvenSense MPU6050
  Mod1 = Raspberry Pi Pico W
  TP1 = TP4056 [chip_label=TP4056 package="DIP (Dual Inline) [THT]"]
  Part2 = ILI9488 TFT SPI 3.5 inch 480x320 w microSD [part_number=MSP3520]
  RE2 = Rotary Encoder [package=THT]  # not connected
  S1 = Toggle Switch [package=THT]
  M1 = MT3608 Module
  Bat1 = battery_holder_single_18650
  RE1 = Rotary Encoder [package=THT]
  R1 = Resistor [tolerance=±5% power=0.25W resistance=100k package=THT]
  R2 = Resistor [tolerance=±5% power=0.25W resistance=100k package=THT]

nets:
  N1: Part1.SCL, Mod1.pin_32
  N2: Part1.SDA, Mod1.pin_31
  N3: Mod1.pin_3, Mod1.pin_8, Mod1.pin_13, Mod1.pin_18, Mod1.pin_23, Mod1.pin_28, Mod1.pin_33, Mod1.pin_38, Part2.GND
  N4: Mod1.pin_4, Part2.LED
  N5: Mod1.pin_5, Part2.DC/RS
  N6: Mod1.pin_6, Part2.RESET
  N7: Mod1.pin_9, Part2.SCK
  N8: Mod1.pin_10, Part2.SDI(MOSI)
  N9: Mod1.pin_12, Part2.CS
  N10: Mod1.pin_15, RE1.EncoderPinB
  N11: Mod1.pin_16, RE1.EncoderPinA
  N12: Mod1.pin_17, RE1.SwitchrPinD
  N13: TP1.pin3, S1.L2
  N14: TP1.pin4, Bat1.+#1
  N15: TP1.pin5, Bat1.+#0
  N16: TP1.pin6, M1.pin1
  N17: S1.COM, M1.pin2, R1.Pin_1
  N18: R1.Pin_0, R2.Pin_0

notes:
  Raised to 5V
  100 kOhm
  Connecting to the power rail ground is easier
  than connecting to the Raspberry Pi's GND pins.

custom parts:
  Raspberry Pi Pico W: Raspberry Pi Pico W. Based around the RP2040 microcontroller the Pico W is a low cost microcontroller device bringing Raspberry Pi quality, cost, and easy of use to the microcontroller space. The areas marked KEEPOUT in pcb silkscreen should not have traces running through them to avoid shorts on a soldered in module!
  TP4056: A DIP stand-in part for whatever IC you want. With 6 pins on a 300mil dual inline package (DIP) footprint.
  ILI9488 TFT SPI 3.5 inch 480x320 w microSD: 3.5" TFT touch display with SPI interface. 24bit RGB color, 480x320 pixels.
  Rotary Encoder: Rotary Encoder from ALPSec11e with switch.
  MT3608 Module: MT3608 Boost Converter Module Links: Aerosemi MT3608 2A Step Up Converter datasheet
  battery_holder_single_18650: single 18650 battery holder
